// Logisim project tp4.circ as structural Verilog
module main (
);

  wire button_1_out, clock_1_out, convertisseur_1_bot, convertisseur_1_center, convertisseur_1_l_h,
       convertisseur_1_l_l, convertisseur_1_r_h, convertisseur_1_r_l, convertisseur_1_top,
       convertisseur_2_bot, convertisseur_2_center, convertisseur_2_l_h, convertisseur_2_l_l,
       convertisseur_2_r_h, convertisseur_2_r_l, convertisseur_2_top, convertisseur_3_bot,
       convertisseur_3_center, convertisseur_3_l_h, convertisseur_3_l_l, convertisseur_3_r_h,
       convertisseur_3_r_l, convertisseur_3_top, lbs_1_c_out, lbs_1_one, lbs_1_three, lbs_1_two, lbs_2_c_out,
       lbs_2_one, lbs_2_three, lbs_2_two, lbs_3_one, lbs_3_three, lbs_3_two;

  Clock clock_1 (.out(clock_1_out));
  Button button_1 (.out(button_1_out));
  LBS lbs_1 (
    .Clock(clock_1_out), .C_in(1'b1), .Reset(button_1_out), .C_out(lbs_1_c_out), .one(lbs_1_one),
    .two(lbs_1_two), .three(lbs_1_three));
  LBS lbs_2 (
    .Clock(clock_1_out), .C_in(lbs_1_c_out), .Reset(button_1_out), .C_out(lbs_2_c_out), .one(lbs_2_one),
    .two(lbs_2_two), .three(lbs_2_three));
  LBS lbs_3 (
    .Clock(clock_1_out), .C_in(lbs_2_c_out), .Reset(button_1_out), .one(lbs_3_one), .two(lbs_3_two),
    .three(lbs_3_three));  // open: C_out
  Convertisseur convertisseur_1 (
    .a(lbs_1_one), .b(lbs_1_two), .c(lbs_1_three), .center(convertisseur_1_center),
    .L_H(convertisseur_1_l_h), .top(convertisseur_1_top), .R_H(convertisseur_1_r_h),
    .R_L(convertisseur_1_r_l), .BOT(convertisseur_1_bot), .L_L(convertisseur_1_l_l));
  Convertisseur convertisseur_2 (
    .a(lbs_2_one), .b(lbs_2_two), .c(lbs_2_three), .center(convertisseur_2_center),
    .L_H(convertisseur_2_l_h), .top(convertisseur_2_top), .R_H(convertisseur_2_r_h),
    .R_L(convertisseur_2_r_l), .BOT(convertisseur_2_bot), .L_L(convertisseur_2_l_l));
  Convertisseur convertisseur_3 (
    .a(lbs_3_one), .b(lbs_3_two), .c(lbs_3_three), .center(convertisseur_3_center),
    .L_H(convertisseur_3_l_h), .top(convertisseur_3_top), .R_H(convertisseur_3_r_h),
    .R_L(convertisseur_3_r_l), .BOT(convertisseur_3_bot), .L_L(convertisseur_3_l_l));
  _7_Segment_Display u_7_segment_display_1 (
    .g(convertisseur_1_center), .f(convertisseur_1_l_h), .a(convertisseur_1_top), .b(convertisseur_1_r_h),
    .e(convertisseur_1_l_l), .d(convertisseur_1_bot), .c(convertisseur_1_r_l), .dp(1'b0));
  _7_Segment_Display u_7_segment_display_2 (
    .g(convertisseur_2_center), .f(convertisseur_2_l_h), .a(convertisseur_2_top), .b(convertisseur_2_r_h),
    .e(convertisseur_2_l_l), .d(convertisseur_2_bot), .c(convertisseur_2_r_l), .dp(1'b0));
  _7_Segment_Display u_7_segment_display_3 (
    .g(convertisseur_3_center), .f(convertisseur_3_l_h), .a(convertisseur_3_top), .b(convertisseur_3_r_h),
    .e(convertisseur_3_l_l), .d(convertisseur_3_bot), .c(convertisseur_3_r_l), .dp(1'b0));
endmodule

module LBS (
  input  Clock,
  input  C_in,
  input  Reset,
  output C_out,
  output one,
  output two,
  output three
);

  wire and_1_out, nand_1_out, or_1_out;

  and and_1 (and_1_out, Clock, C_in);
  nand nand_1 (nand_1_out, or_1_out, Clock);
  or or_1 (or_1_out, three, two, one);
  D_Flip_Flop d_ff_1 (.D(nand_1_out), .clk(and_1_out), .Q(one), .reset(Reset));  // open: Qn, preset
  D_Flip_Flop d_ff_2 (.D(one), .clk(and_1_out), .Q(two), .reset(Reset));  // open: Qn, preset
  D_Flip_Flop d_ff_3 (.D(two), .clk(and_1_out), .Q(three), .reset(Reset));  // open: Qn, preset
  and and_2 (C_out, C_in, three);
endmodule

module Convertisseur (
  input  a,
  input  b,
  input  c,
  output center,
  output L_H,
  output top,
  output R_H,
  output R_L,
  output BOT,
  output L_L
);

  wire not_1_out, not_2_out;

  not not_1 (not_1_out, b);
  not not_2 (not_2_out, c);
  not not_3 (top, b);
  not not_4 (R_L, c);
  not not_5 (BOT, b);
  not not_6 (L_L, b);
  and and_1 (L_H, not_1_out, not_2_out);

  assign center = c;
  assign R_H = 1'b1;
endmodule
